# Fritzing sketch MinimalPiClock (saved by Fritzing 1.0.1rc)
circuit board: 16cm x 10cm
breadboards: 1

parts:
  C2 = Capacitor [package=cap-pth-small2]
  Y1 = CRYSTAL [package=crystal-smd-10.5x4.8-2pin]
  BEEP = Piezo Speaker
  A2 = atmega328 [package=dip]
  X1 = USB Connectors [package=usb-b-smt]
  C1 = Capacitor [package=cap-pth-small2]

nets:
  N1: C2.1, Y1.2, A2.XLAT2
  GND: C2.2, BEEP.pin1, A2.GND, X1.GND, C1.2
  N2: Y1.1, A2.XLAT1, C1.1
  N3: BEEP.pin2, A2.D8
  N4: A2.VCC, A2.AVCC, A2.AREF, X1.VBUS

notes:
  Capacitors: 22 pF
  Crystal: 16 MHz
  5 volt in any way
